# Fritzing sketch Blink_Timer_External_Clock (saved by Fritzing 0.9.6b)
breadboards: 1

parts:
  IC1 = IC, DIP package, 20 pins [chip_label=MSP430G2452]
  LED1 = LED - 5mm [color="Green (565nm)" current=0.030 package="5 mm [THT]"]
  R1 = Resistor [tolerance=±5% power=0.25 resistance=220 package=THT]
  J1 = Dagu DGServo 9g header (male) [package=THT]
  eZ-FET = Dagu DGServo 9g header (male) [package=THT]
  R2 = Resistor [tolerance=±5% resistance=47k package="0603 [SMD]"]
  Y1 = CRYSTAL [package=crystal-32khz-smd_epson_mc146]
  1nF = Capacitor [package=cap-pth-5mm]

nets:
  N1: IC1.pin1, J1.gnd, R2.Pin_0
  N2: IC1.pin10, LED1.anode
  N3: IC1.pin16, J1.pulse, R2.Pin_1, 1nF.2
  N4: IC1.pin17, J1.Vcc
  N5: IC1.pin18, Y1.2
  N6: IC1.pin19, Y1.1
  N7: IC1.pin20, LED1.cathode, R1.Pin_0, eZ-FET.gnd, 1nF.1

notes:
  eZ-FET conections:
  VCC SBWTCK SWDTDIO GND
