# Fritzing sketch msp430g2_buzzer (saved by Fritzing 0.9.6b)
breadboards: 1

parts:
  IC1 = IC, DIP package, 20 pins [chip_label=MSP430G2452]
  J1 = Dagu DGServo 9g header (male) [package=THT]
  eZ-FET = Dagu DGServo 9g header (male) [package=THT]
  R2 = Resistor [tolerance=±5% resistance=47k package="0603 [SMD]"]
  1nF = Capacitor [package=cap-pth-5mm]
  S1 = Momentary Switch [package=ksa_sealed_tac_switch]
  J2 = Piezo Speaker
  C1 = Film/Foil Capacitor [capacitance=100nF voltage=35V package="5mm [THT, pp]"]

nets:
  N1: IC1.pin1, J1.gnd, R2.Pin_0, C1.+
  N2: IC1.pin9, S1.4, C1.-
  N3: IC1.pin10, J2.pin2
  N4: IC1.pin16, J1.pulse, R2.Pin_1, 1nF.2
  N5: IC1.pin17, J1.Vcc
  N6: IC1.pin20, eZ-FET.gnd, 1nF.1, J2.pin1

notes:
  eZ-FET conections:
  GND SBWTCK SWDTDIO VCC
  eZ430-RF2500:
  GND TEST RST VCC
